// Digital circuit 2_to_1_mux.dig as structural Verilog
module _2_to_1_mux (
  input  A,
  input  B,
  input  S,
  output Q
);

  wire and_1_out, and_2_out, not_1_out;

  not not_1 (not_1_out, S);
  and and_1 (and_1_out, A, not_1_out);
  and and_2 (and_2_out, B, S);
  or or_1 (Q, and_1_out, and_2_out);
endmodule

/* Test case MUX:
A B S Q
0 0 0 0
0 0 1 0
0 1 0 0
0 1 1 1
1 0 0 1
1 0 1 0
1 1 0 1
1 1 1 1
*/
