// Digital circuit 2_to_1_wide_mux.dig as structural Verilog
module _2_to_1_wide_mux (
  input  [3:0] A,
  input  [3:0] B,
  input  SEL,
  output [3:0] Q
);

  _2_to_1_mux _2_to_1_mux_1 (.A(A[0]), .B(B[0]), .S(SEL), .Q(Q[0]));
  _2_to_1_mux _2_to_1_mux_2 (.A(A[1]), .B(B[1]), .S(SEL), .Q(Q[1]));
  _2_to_1_mux _2_to_1_mux_3 (.A(A[2]), .B(B[2]), .S(SEL), .Q(Q[2]));
  _2_to_1_mux _2_to_1_mux_4 (.A(A[3]), .B(B[3]), .S(SEL), .Q(Q[3]));
endmodule

/* Test case:
    A B SEL Q
loop(i, 15)
    loop(j, 15)
    (i) (j) (0) (i)
    (i) (j) (1) (j)
    end loop
end loop
*/
