// Digital circuit 4_to_1_mux.dig as structural Verilog
module _4_to_1_mux (
  input  A,
  input  B,
  input  C,
  input  D,
  input  [1:0] S,
  output Q
);

  wire _2_to_1_mux_1_q, _2_to_1_mux_2_q;

  _2_to_1_mux _2_to_1_mux_1 (.A(A), .B(B), .S(S[0]), .Q(_2_to_1_mux_1_q));
  _2_to_1_mux _2_to_1_mux_2 (.A(C), .B(D), .S(S[0]), .Q(_2_to_1_mux_2_q));
  _2_to_1_mux _2_to_1_mux_3 (.A(_2_to_1_mux_1_q), .B(_2_to_1_mux_2_q), .S(S[1]), .Q(Q));
endmodule

/* Test case:
A B C D S   Q
0 X X X 00  0
1 X X X 00  1
X 0 X X 01  0
X 1 X X 01  1
X X 0 X 10  0
X X 1 X 10  1
X X X 0 11  0
X X X 1 11  1
*/
