// Digital circuit 4_to_1_wide_mux.dig as structural Verilog
module _4_to_1_wide_mux (
  input  [3:0] A,
  input  [3:0] B,
  input  [3:0] C,
  input  [3:0] D,
  input  [1:0] S,
  output [3:0] Q
);

  _4_to_1_mux _4_to_1_mux_1 (.A(A[0]), .B(B[0]), .C(C[0]), .D(D[0]), .S(S), .Q(Q[0]));
  _4_to_1_mux _4_to_1_mux_2 (.A(A[1]), .B(B[1]), .C(C[1]), .D(D[1]), .S(S), .Q(Q[1]));
  _4_to_1_mux _4_to_1_mux_3 (.A(A[2]), .B(B[2]), .C(C[2]), .D(D[2]), .S(S), .Q(Q[2]));
  _4_to_1_mux _4_to_1_mux_4 (.A(A[3]), .B(B[3]), .C(C[3]), .D(D[3]), .S(S), .Q(Q[3]));
endmodule

/* Test case:
    A B C D S Q
loop(i, 250)
    let x = random(1<<4);
    let y = random(1<<4);
    let z = random(1<<4);
    let w = random(1<<4);
    (x) (y) (z) (w) (00) (x)
    (x) (y) (z) (w) (01) (y)
    (x) (y) (z) (w) (10) (z)
    (x) (y) (z) (w) (11) (w)
end loop
*/
