// Digital circuit mux_emulate_xor.dig as structural Verilog
module mux_emulate_xor (
  input  A,
  input  B,
  output Q
);

  _4_to_1_mux _4_to_1_mux_1 (.A(1'b0), .B(1'b1), .C(1'b1), .D(1'b0), .Q(Q), .S({B, A}));
endmodule

/* Test case is XOR?:
A B Q
0 0 0
0 1 1
1 0 1
1 1 0
*/
