// Digital circuit shift.dig as structural Verilog
module shift (
  input  [7:0] A,
  output [7:0] B
);


  assign B = {A[6:0], 1'b0};
endmodule

/* Test case:
    A    B
loop(i, 256)
    (i)  (i<<1)
end loop
*/
