// Digital circuit adder-subtracter.dig as structural Verilog
module adder_subtracter (
  input  [3:0] A,
  input  [3:0] B,
  input  SUB,
  output [3:0] Q
);

  wire add_2_c_o, add_3_c_o, add_4_c_o, xor_1_out, xor_2_out, xor_3_out, xor_4_out;

  xor xor_1 (xor_1_out, B[3], SUB);
  Add add_1 (.a(A[3]), .b(xor_1_out), .c_i(add_2_c_o), .s(Q[3]));  // open: c_o
  xor xor_2 (xor_2_out, B[2], SUB);
  Add add_2 (.a(A[2]), .b(xor_2_out), .c_i(add_3_c_o), .s(Q[2]), .c_o(add_2_c_o));
  xor xor_3 (xor_3_out, B[1], SUB);
  Add add_3 (.a(A[1]), .b(xor_3_out), .c_i(add_4_c_o), .s(Q[1]), .c_o(add_3_c_o));
  xor xor_4 (xor_4_out, B[0], SUB);
  Add add_4 (.a(A[0]), .b(xor_4_out), .c_i(SUB), .s(Q[0]), .c_o(add_4_c_o));

  // Notes on the sheet:
  //   A: First adder input
  //   B: Second adder input
  //   SUB: Selection bit to enable subtract mode.
  //   If set high, the unit should perform a subtraction.
  //   Q: Result of adding A and B
endmodule

/* Test case Add:
SUB A B Q

loop(a, 1 << 4)
loop(b, 1 << 4)

0 (a) (b) ((a + b) & 0xF)

end loop
end loop
*/

/* Test case Sub:
SUB A B Q

loop(a, 1 << 4)
loop(b, 1 << 4)

1 (a) (b) ((a - b) & 0xF)

end loop
end loop
*/
