// Digital circuit and.dig as structural Verilog
module \and  (
  input  [3:0] A,
  input  [3:0] B,
  output [3:0] Q
);

  assign Q = A & B;  // And and_1, 4 bits wide

  // Notes on the sheet:
  //   A: First input
  //   B: Second input
  //   Q: Result of A AND B
endmodule

/* Test case AND:
A B Q

loop(a, 1 << 4)
loop(b, 1 << 4)

(a) (b) (a & b)

end loop
end loop
*/
