// Digital circuit full-adder.dig as structural Verilog
module full_adder (
  input  A,
  input  B,
  input  C_IN,
  output Q,
  output C_OUT
);

  wire half_adder_1_c, half_adder_1_q, half_adder_2_c;

  half_adder half_adder_1 (.A(A), .B(B), .Q(half_adder_1_q), .C(half_adder_1_c));
  half_adder half_adder_2 (.A(half_adder_1_q), .B(C_IN), .Q(Q), .C(half_adder_2_c));
  or or_1 (C_OUT, half_adder_1_c, half_adder_2_c);

  // Notes on the sheet:
  //   A: First bit input
  //   B: Second bit input
  //   C_IN: Input carry bit
  //   Q: Result of adding A, B, and C_IN
  //   C_OUT: Bit to indicate a carry occurred when adding A, B, and C_IN
endmodule

/* Test case Full-adder:
A B C_IN Q C_OUT
0 0 0 0 0
0 0 1 1 0
0 1 0 1 0
0 1 1 0 1
1 0 0 1 0
1 0 1 0 1
1 1 0 0 1
1 1 1 1 1
*/
