// Digital circuit ripple-carry-adder.dig as structural Verilog
module ripple_carry_adder (
  input  [3:0] A,
  input  [3:0] B,
  output [3:0] Q
);

  wire full_adder_1_c_out, full_adder_2_c_out, full_adder_3_c_out;

  full_adder full_adder_1 (.A(A[0]), .B(B[0]), .C_IN(1'b0), .Q(Q[0]), .C_OUT(full_adder_1_c_out));
  full_adder full_adder_2 (.A(A[1]), .B(B[1]), .C_IN(full_adder_1_c_out), .Q(Q[1]), .C_OUT(full_adder_2_c_out));
  full_adder full_adder_3 (.A(A[2]), .B(B[2]), .C_IN(full_adder_2_c_out), .Q(Q[2]), .C_OUT(full_adder_3_c_out));
  full_adder full_adder_4 (.A(A[3]), .B(B[3]), .C_IN(full_adder_3_c_out), .Q(Q[3]));  // open: C_OUT

  // Notes on the sheet:
  //   A: First adder input
  //   B: Second adder input
  //   Q: Result of adding A and B
endmodule

/* Test case Adder:
A B Q

loop(a, 1 << 4)
loop(b, 1 << 4)

(a) (b) ((a + b) & 0xF)

end loop
end loop
*/
