// Digital circuit counter.dig as structural Verilog
module counter (
  input  [15:0] D,
  input  ld,
  input  clk,
  output [15:0] Q
);

  wire [15:0] add_1_s, multiplexer_1_out;

  Multiplexer #(.Bits(16)) multiplexer_1 (.sel(ld), .in_0(Q), .in_1(D), .out(multiplexer_1_out));
  Add #(.Bits(16)) add_1 (.a(multiplexer_1_out), .b(16'h1), .c_i(1'b0), .s(add_1_s));  // open: c_o
  Register #(.Bits(16)) register_1 (.D(add_1_s), .C(clk), .en(1'b1), .Q(Q));
endmodule

/* Test case:
clk ld D Q

0 0 0 0
c 0 0 0x1
c 0 0 0x2
c 1 0 0x1
c 1 0 0x1
c 1 0x1 0x2
c 1 0xA 0xB
c 1 0xE 0xF
*/
