// Digital circuit d_flipflop.dig as structural Verilog
module d_flipflop (
  input  clk,
  input  D,
  output Q
);

  wire d_latch_1_q, not_1_out;

  not not_1 (not_1_out, clk);
  d_latch d_latch_1 (.en(not_1_out), .D(D), .Q(d_latch_1_q));
  d_latch d_latch_2 (.en(clk), .D(d_latch_1_q), .Q(Q));
endmodule

/* Test case:
clk D Q
0 0 x
1 0 0
1 1 0
1 1 0
0 1 0
0 0 0
0 1 0
1 1 1
1 0 1
1 0 1
0 0 1
0 0 1
0 1 1
1 1 1
1 0 1
1 0 1
0 0 1
0 0 1
0 0 1
1 0 0
*/
