// Digital circuit d_flipflop_with_en.dig as structural Verilog
module d_flipflop_with_en (
  input  clk,
  input  D,
  input  en,
  output Q
);

  wire multiplexer_1_out;

  Multiplexer multiplexer_1 (.sel(en), .in_0(Q), .in_1(D), .out(multiplexer_1_out));
  d_flipflop d_flipflop_1 (.clk(clk), .D(multiplexer_1_out), .Q(Q));
endmodule

/* Test case:
clk en D Q
0 1 0 x
1 1 0 0
1 1 0 0
0 1 0 0
0 1 1 0
1 1 1 1
1 1 1 1
0 1 1 1
0 1 0 1
1 1 0 0
1 1 0 0
0 1 0 0
0 0 1 0
1 0 1 0
1 0 1 0
0 0 0 0
0 1 1 0
1 1 1 1
1 1 0 1
0 1 0 1
0 0 0 1
1 0 0 1
1 1 0 1
0 1 0 1
0 1 0 1
*/
