// Digital circuit d_latch.dig as structural Verilog
module d_latch (
  input  en,
  input  D,
  output Q
);

  wire and_1_out, and_2_out, not_1_out;

  not not_1 (not_1_out, D);
  and and_1 (and_1_out, en, not_1_out);
  and and_2 (and_2_out, en, D);
  sr_latch sr_latch_1 (.R(and_1_out), .S(and_2_out), .Q(Q));
endmodule

/* Test case:
en D Q
0 0 x
1 0 0
0 0 0
1 1 1
0 1 1
0 0 1
1 0 0
1 1 1
0 1 1
0 0 1
1 1 1
0 0 1
*/
