// Digital circuit incrementer.dig as structural Verilog
module incrementer (
  input  clk
);

  wire [3:0] add_1_s, d_flipflop_1_q;

  Add #(.Bits(4)) add_1 (.a(d_flipflop_1_q), .b(4'b0001), .c_i(1'b0), .s(add_1_s));  // open: c_o
  d_flipflop d_flipflop_1 (.clk(clk), .D(add_1_s[0]), .Q(d_flipflop_1_q[0]));
  d_flipflop d_flipflop_2 (.clk(clk), .D(add_1_s[1]), .Q(d_flipflop_1_q[1]));
  d_flipflop d_flipflop_3 (.clk(clk), .D(add_1_s[2]), .Q(d_flipflop_1_q[2]));
  d_flipflop d_flipflop_4 (.clk(clk), .D(add_1_s[3]), .Q(d_flipflop_1_q[3]));
endmodule
