// Digital circuit reg_file.dig as structural Verilog
module reg_file (
  input  [2:0] RS1,
  input  [2:0] RS2,
  input  [2:0] WS,
  input  WE,
  input  [15:0] IN,
  input  clk,
  output [15:0] OUT1,
  output [15:0] OUT2
);

  wire and_1_out, and_2_out, and_3_out, and_4_out, decoder_1_out_1, decoder_1_out_2, decoder_1_out_3,
       decoder_1_out_4;
  wire [15:0] notconnected_1_out, notconnected_2_out, notconnected_3_out, notconnected_4_out,
       notconnected_5_out, notconnected_6_out, register_1_q, register_2_q, register_3_q, register_4_q;

  Decoder #(.Selector_Bits(3)) decoder_1 (
    .sel(WS), .out_1(decoder_1_out_1), .out_2(decoder_1_out_2), .out_3(decoder_1_out_3),
    .out_4(decoder_1_out_4));  // open: out_0, out_5, out_6, out_7
  and and_1 (and_1_out, clk, decoder_1_out_1);
  and and_2 (and_2_out, clk, decoder_1_out_2);
  and and_3 (and_3_out, clk, decoder_1_out_3);
  and and_4 (and_4_out, clk, decoder_1_out_4);
  Register #(.Bits(16)) register_1 (.D(IN), .C(and_1_out), .en(WE), .Q(register_1_q));
  Register #(.Bits(16)) register_2 (.D(IN), .C(and_2_out), .en(WE), .Q(register_2_q));
  Register #(.Bits(16)) register_3 (.D(IN), .C(and_3_out), .en(WE), .Q(register_3_q));
  Register #(.Bits(16)) register_4 (.D(IN), .C(and_4_out), .en(WE), .Q(register_4_q));
  Multiplexer #(.Bits(16), .Selector_Bits(3)) multiplexer_1 (
    .sel(RS1), .in_0({16{1'b0}}), .in_1(register_1_q), .in_2(register_2_q), .in_3(register_3_q),
    .in_4(register_4_q), .in_5(notconnected_1_out), .in_6(notconnected_2_out), .in_7(notconnected_3_out),
    .out(OUT1));
  // NotConnected on notconnected_1_out
  // NotConnected on notconnected_2_out
  // NotConnected on notconnected_3_out
  Multiplexer #(.Selector_Bits(3), .Bits(16)) multiplexer_2 (
    .sel(RS2), .in_0({16{1'b0}}), .in_1(register_1_q), .in_2(register_2_q), .in_3(register_3_q),
    .in_4(register_4_q), .in_5(notconnected_4_out), .in_6(notconnected_5_out), .in_7(notconnected_6_out),
    .out(OUT2));
  // NotConnected on notconnected_4_out
  // NotConnected on notconnected_5_out
  // NotConnected on notconnected_6_out

  // Notes on the sheet:
  //   RS1: The index of the register which should output its value to OUT1.
  //   RS2: The index of the register which should output its value to OUT2.
  //   WS: The index of the register which should save the value on IN on the next clock cycle (if WE is high).
  //   WE: Whether the register selected by WS should save the value from IN on the next cycle.
  //   IN: The value to be saved into the register specified by WS if WE is high,
  //   OUT1: The value in the register specified by RS1.
  //   OUT2: The value in the register specified by RS2.
endmodule

/* Test case:
clk RS1 RS2 WS WE IN OUT1 OUT2
c 0 0 0 1 0x1234 0x1234 0x1234
c 1 0 1 1 0xBEEF 0xBEEF 0x1234
c 2 1 2 1 0xDEAD 0xDEAD 0xBEEF
c 3 2 3 1 0xFFFF 0xFFFF 0xDEAD
c 3 2 3 0 0xABCD 0xFFFF 0xDEAD
c 3 2 2 0 0xABCD 0xFFFF 0xDEAD
c 1 0 1 0 0xABCD 0xBEEF 0x1234
c 1 0 0 0 0xABCD 0xBEEF 0x1234
c 1 0 2 1 0xBADE 0xBEEF 0x1234
c 0 2 2 1 0xBADE 0x1234 0xBADE
c 0 0 2 0 0x1234 0x1234 0x1234
c 2 3 0 1 0x0000 0xBADE 0xFFFF
c 0 0 2 0 0x1234 0x0000 0x0000
*/
