// Digital circuit register.dig as structural Verilog
module register (
  input  [15:0] D,
  input  clk,
  input  en,
  output [15:0] Q
);

  d_flipflop_with_en d_flipflop_with_en_1 (.clk(clk), .D(D[0]), .en(en), .Q(Q[0]));
  d_flipflop_with_en d_flipflop_with_en_2 (.clk(clk), .D(D[2]), .en(en), .Q(Q[2]));
  d_flipflop_with_en d_flipflop_with_en_3 (.clk(clk), .D(D[4]), .en(en), .Q(Q[4]));
  d_flipflop_with_en d_flipflop_with_en_4 (.clk(clk), .D(D[6]), .en(en), .Q(Q[6]));
  d_flipflop_with_en d_flipflop_with_en_5 (.clk(clk), .D(D[8]), .en(en), .Q(Q[8]));
  d_flipflop_with_en d_flipflop_with_en_6 (.clk(clk), .D(D[10]), .en(en), .Q(Q[10]));
  d_flipflop_with_en d_flipflop_with_en_7 (.clk(clk), .D(D[12]), .en(en), .Q(Q[12]));
  d_flipflop_with_en d_flipflop_with_en_8 (.clk(clk), .D(D[14]), .en(en), .Q(Q[14]));
  d_flipflop_with_en d_flipflop_with_en_9 (.clk(clk), .D(D[1]), .en(en), .Q(Q[1]));
  d_flipflop_with_en d_flipflop_with_en_10 (.clk(clk), .D(D[3]), .en(en), .Q(Q[3]));
  d_flipflop_with_en d_flipflop_with_en_11 (.clk(clk), .D(D[5]), .en(en), .Q(Q[5]));
  d_flipflop_with_en d_flipflop_with_en_12 (.clk(clk), .D(D[7]), .en(en), .Q(Q[7]));
  d_flipflop_with_en d_flipflop_with_en_13 (.clk(clk), .D(D[9]), .en(en), .Q(Q[9]));
  d_flipflop_with_en d_flipflop_with_en_14 (.clk(clk), .D(D[11]), .en(en), .Q(Q[11]));
  d_flipflop_with_en d_flipflop_with_en_15 (.clk(clk), .D(D[13]), .en(en), .Q(Q[13]));
  d_flipflop_with_en d_flipflop_with_en_16 (.clk(clk), .D(D[15]), .en(en), .Q(Q[15]));
endmodule
