// Digital circuit sr_latch.dig as structural Verilog
module sr_latch (
  input  R,
  input  S,
  output Q
);

  wire nor_2_out;

  nor nor_1 (Q, R, nor_2_out);
  nor nor_2 (nor_2_out, Q, S);
endmodule

/* Test case:
R S Q
0 0 x
1 0 0
0 0 0
0 1 1
0 0 1
0 1 1
1 0 0
0 0 0
*/
