// Digital circuit calc.dig as structural Verilog
module calc (
  input  [2:0] RS1,
  input  [2:0] RS2,
  input  [2:0] WS,
  input  WE,
  input  CLK,
  input  [1:0] ALUOP,
  output Z,
  output N,
  output C,
  output V
);

  wire [15:0] ALU_result, Register_File_out1, Register_File_out2;

  reg_file Register_File (
    .IN(ALU_result), .clk(CLK), .RS1(RS1), .RS2(RS2), .WS(WS), .WE(WE), .OUT1(Register_File_out1),
    .OUT2(Register_File_out2));
  alu ALU (.A(Register_File_out1), .B(Register_File_out2), .RESULT(ALU_result), .ALUOP(ALUOP), .FLAG({V, C, N, Z}));
  // Probe RESULT on ALU_result
endmodule

/* Test case Calc:
# Testing the simple manual calculator
# CLK: Clock
# ALUOP: ALU opcode
# RS1: First operand
# RS2: Second operand
# RD: Destination register to write to
# WE: Write enable
# R0-R3: Registers

CLK ALUOP RS1 RS2 WS WE    R1 R2 R3 R4

init R1=1;
init R2=3;
init R3=0xF;

0   0    0   0   0  0      1  3  0xF 0       #ensure registers initalised correctly
C   x    x   x   x  0      1  3  0xF 0       #do nothing
C   0    1   3   4  1      x  x  x   0x10    #R4 = 0x10
C   1    3   2   4  1      x  x  x   0xC     #R4 = 0xC
C   1    0   1   4  1      x  x  x   0xFFFF  #R4 = 0xFFFF
*/
