// Digital circuit load_and_store.dig as structural Verilog
module load_and_store (
  input  CLK,
  input  [2:0] RS1,
  input  [2:0] RS2,
  input  [2:0] WS,
  input  STR,
  input  LDR,
  input  WE
);

  wire [15:0] RAM_d, reg_file_1_out1, reg_file_1_out2;

  reg_file reg_file_1 (
    .IN(RAM_d), .clk(CLK), .RS1(RS1), .RS2(RS2), .WS(WS), .WE(WE), .OUT1(reg_file_1_out1),
    .OUT2(reg_file_1_out2));
  RAMDualPort #(.AddrBits(16), .isProgramMemory("true"), .Bits(16)) RAM (
    .A(reg_file_1_out1), .Din(reg_file_1_out2), .str(STR), .C(CLK), .ld(LDR), .D(RAM_d));
endmodule
