// Digital circuit manual_cpu.dig as structural Verilog
module manual_cpu (
  input  CLK,
  input  [2:0] RS1,
  input  [2:0] RS2,
  input  [2:0] WS,
  input  STR,
  input  LDR,
  input  WE,
  input  [15:0] IN,
  input  [1:0] ALUOP,
  input  [1:0] DMUX,
  output Z,
  output N,
  output C,
  output V
);

  wire [15:0] alu_1_result, multiplexer_1_out, notconnected_1_out, RAM_d, reg_file_1_out1, reg_file_1_out2;

  Multiplexer #(.Selector_Bits(2), .Bits(16)) multiplexer_1 (
    .sel(DMUX), .in_0(alu_1_result), .in_1(RAM_d), .in_2(IN), .in_3(notconnected_1_out),
    .out(multiplexer_1_out));
  // NotConnected on notconnected_1_out
  RAMDualPort #(.AddrBits(16), .isProgramMemory("true"), .Bits(16)) RAM (
    .A(reg_file_1_out1), .Din(reg_file_1_out2), .str(STR), .C(CLK), .ld(LDR), .D(RAM_d));
  // Probe DATA on multiplexer_1_out
  reg_file reg_file_1 (
    .IN(multiplexer_1_out), .clk(CLK), .RS1(RS1), .RS2(RS2), .WS(WS), .WE(WE), .OUT1(reg_file_1_out1),
    .OUT2(reg_file_1_out2));
  alu alu_1 (.A(reg_file_1_out1), .B(reg_file_1_out2), .RESULT(alu_1_result), .ALUOP(ALUOP), .FLAG({V, C, N, Z}));
endmodule

/* Test case Manual CPU:
# Testing the manual CPU
# CLK: Clock
# ALUOP: ALU opcode
#    00 - ADD, 01 - SUB, 10 - AND, 11 - ORR
# RS1: First operand
# RS2: Second operand
# WS: Destination register to write to
# WE: (Register) Write enable
# STR: Store
# LDR: Load
# R1-R4: Registers
# DATA: Output from Data Multiplexer
#  00 - ALU, 01 - MEMORY, 10-INPUT, 11-X
# IN: Manual data input
CLK ALUOP RS1 RS2 WS WE STR LDR IN DMUX    R1 R2 R3     R4     DATA

program(0xAAAA, 0xBBBB, 0xCCCC, 0xDDDD)

0   0     0   0   0  0  0   0   0  x       x  x  x      x      x      # registers uninitalised
C   x     x   x   1  1  0   0   1  2       1  x  x      x      1      # R1 := 1
C   x     x   x   2  1  0   0   2  2       1  2  x      x      2      # R2 := 2
C   x     0   x   3  1  0   1   0  1       1  2  0xAAAA x      0xAAAA # R3 := mem[RZ]
C   x     1   x   4  1  0   1   0  1       1  2  0xAAAA 0xBBBB 0xBBBB # R4 := mem[R1]
C   0     3   4   4  1  0   0   0  0       1  2  0xAAAA 0x6665 x      # R4 := R4 + R3
C   x     2   4   x  0  1   0   0  x       1  2  0xAAAA 0x6665 x      # mem[R2] := R4
C   x     2   x   x  0  0   1   0  1       1  2  0xAAAA 0x6665 0x6665 # check mem[R2] := R4
*/
