// Digital circuit control_unit.dig as structural Verilog
module control_unit (
  input  [15:0] INST,
  output [1:0] ALUOP,
  output [1:0] DMUX,
  output [2:0] RS1,
  output [2:0] RS2,
  output [2:0] WS,
  output WE,
  output STR,
  output LDR
);

  wire and_3_out, not_1_out, not_2_out, not_3_out;

  Multiplexer #(.Selector_Bits(4)) multiplexer_1 (
    .sel(INST[15:12]), .in_0(1'b1), .in_1(1'b1), .in_2(1'b1), .in_3(1'b1), .in_4(1'b1), .in_5(1'b0),
    .in_6(1'b1), .in_7(1'b1), .in_8(1'b0), .in_9(1'b0), .in_10(1'b0), .in_11(1'b0), .in_12(1'b1),
    .in_13(1'b1), .in_14(1'b1), .in_15(1'b1), .out(DMUX[1]));
  and and_1 (ALUOP[1], INST[13], INST[15]);
  Multiplexer #(.Selector_Bits(4)) multiplexer_2 (
    .sel(INST[15:12]), .in_0(1'b0), .in_1(1'b1), .in_2(1'b1), .in_3(1'b1), .in_4(1'b1), .in_5(1'b1),
    .in_6(1'b1), .in_7(1'b1), .in_8(1'b0), .in_9(1'b0), .in_10(1'b0), .in_11(1'b0), .in_12(1'b1),
    .in_13(1'b1), .in_14(1'b1), .in_15(1'b1), .out(DMUX[0]));
  and and_2 (ALUOP[0], INST[12], INST[15]);
  not not_1 (not_1_out, INST[13]);
  not not_2 (not_2_out, INST[15]);
  and and_3 (and_3_out, not_1_out, INST[14], not_2_out);
  not not_3 (not_3_out, INST[12]);
  and and_4 (LDR, INST[12], and_3_out);
  and and_5 (STR, and_3_out, not_3_out);
  Multiplexer #(.Bits(3)) multiplexer_3 (.sel(STR), .in_0(INST[2:0]), .in_1(INST[10:8]), .out(RS2));
  not not_4 (WE, STR);

  assign RS1 = INST[6:4];
  assign WS = INST[10:8];

  // Notes on the sheet:
  //   Z
  //   Rd
  //   Ra
  //   Rb
  //   opcode
endmodule

/* Test case All Tests:
	INST                                    WE  ALUOP  RS1   RS2  WS  STR  LDR DMUX

let aluop  = 0b1000;
let ldrop  = 0b0101;
let strop  = 0b0100;
let movlop = 0b0000;

loop(rd, 1<<3)
loop(ra, 1<<3)
loop(rb, 1<<3)

loop(i, 4)
	((aluop+i)<<12 | rd<<8 | ra<<4 | rb<<0) 1  (i)     (ra)  (rb) (rd)  0   X    0  #test add/sub/and/orr
end loop

	(ldrop    <<12 | rd<<8 | ra<<4 )        1  X       (ra)  x    (rd)  0   1    1  #test ldr
	(strop    <<12 | rd<<8 | ra<<4 )        0  X       (ra)  (rd)  X    1   X    X  #test str
	
	let imm = random(256);
	(movlop   <<12 | rd<<8 | imm )          1  X       X      X   (rd)  0   X    2  #test movl

end loop
end loop
end loop
*/

/* Test case WS:
	INST                                    WS 

let aluop  = 0b1000;
let ldrop  = 0b0101;
let strop  = 0b0100;
let movlop = 0b0000;

loop(rd, 1<<3)
loop(ra, 1<<3)
loop(rb, 1<<3)

loop(i, 4)
	((aluop+i)<<12 | rd<<8 | ra<<4 | rb<<0) (rd)  #test add/sub/and/orr
end loop

	(ldrop    <<12 | rd<<8 | ra<<4 )        (rd)   #test ldr
	(strop    <<12 | rd<<8 | ra<<4 )        X     #test str
	
	let imm = random(256);
	(movlop   <<12 | rd<<8 | imm )          (rd)  #test movl

end loop
end loop
end loop
*/

/* Test case RS1:
	INST                                    RS1  

let aluop  = 0b1000;
let ldrop  = 0b0101;
let strop  = 0b0100;
let movlop = 0b0000;

loop(rd, 1<<3)
loop(ra, 1<<3)
loop(rb, 1<<3)

loop(i, 4)
	((aluop+i)<<12 | rd<<8 | ra<<4 | rb<<0) (ra)  #test add/sub/and/orr
end loop

	(ldrop    <<12 | rd<<8 | ra<<4 )        (ra)  #test ldr
	(strop    <<12 | rd<<8 | ra<<4 )        (ra)  #test str

end loop
end loop
end loop
*/

/* Test case RS2:
	INST                                    RS2  

let aluop  = 0b1000;
let ldrop  = 0b0101;
let strop  = 0b0100;
let movlop = 0b0000;

loop(rd, 1<<3)
loop(ra, 1<<3)
loop(rb, 1<<3)

loop(i, 4)
	((aluop+i)<<12 | rd<<8 | ra<<4 | rb<<0) (rb) #test add/sub/and/orr
end loop
	(strop    <<12 | rd<<8 | ra<<4 )        (rd) #test str

end loop
end loop
end loop
*/

/* Test case LDR:
	INST                                    LDR 

let aluop  = 0b1000;
let ldrop  = 0b0101;
let strop  = 0b0100;
let movlop = 0b0000;

loop(rd, 1<<3)
loop(ra, 1<<3)
loop(rb, 1<<3)

loop(i, 4)
	((aluop+i)<<12 | rd<<8 | ra<<4 | rb<<0) X    #test add/sub/and/orr
end loop

	(ldrop    <<12 | rd<<8 | ra<<4 )        1    #test ldr
	(strop    <<12 | rd<<8 | ra<<4 )        X    #test str
	
	let imm = random(256);
	(movlop   <<12 | rd<<8 | imm )          X    #test movl

end loop
end loop
end loop
*/

/* Test case STR:
	INST                                    STR 

let aluop  = 0b1000;
let ldrop  = 0b0101;
let strop  = 0b0100;
let movlop = 0b0000;

loop(rd, 1<<3)
loop(ra, 1<<3)
loop(rb, 1<<3)

loop(i, 4)
	((aluop+i)<<12 | rd<<8 | ra<<4 | rb<<0) 0  #test add/sub/and/orr
end loop

	(ldrop    <<12 | rd<<8 | ra<<4 )        0  #test ldr
	(strop    <<12 | rd<<8 | ra<<4 )        1  #test str
	
	let imm = random(256);
	(movlop   <<12 | rd<<8 | imm )          0  #test movl

end loop
end loop
end loop
*/

/* Test case WE:
	INST                                    WE  

let aluop  = 0b1000;
let ldrop  = 0b0101;
let strop  = 0b0100;
let movlop = 0b0000;

loop(rd, 1<<3)
loop(ra, 1<<3)
loop(rb, 1<<3)

loop(i, 4)
	((aluop+i)<<12 | rd<<8 | ra<<4 | rb<<0) 1  #test add/sub/and/orr
end loop

	(ldrop    <<12 | rd<<8 | ra<<4 )        1  #test ldr
	(strop    <<12 | rd<<8 | ra<<4 )        0  #test str
	
	let imm = random(256);
	(movlop   <<12 | rd<<8 | imm )          1  #test movl

end loop
end loop
end loop
*/

/* Test case ALUOP:
	INST                                    ALUOP 

let aluop  = 0b1000;
let ldrop  = 0b0101;
let strop  = 0b0100;
let movlop = 0b0000;

loop(rd, 1<<3)
loop(ra, 1<<3)
loop(rb, 1<<3)

loop(i, 4)
	((aluop+i)<<12 | rd<<8 | ra<<4 | rb<<0) (i)    #test add/sub/and/orr
end loop

end loop
end loop
end loop
*/

/* Test case DMUX:
	INST                                    DMUX

let aluop  = 0b1000;
let ldrop  = 0b0101;
let strop  = 0b0100;
let movlop = 0b0000;

loop(rd, 1<<3)
loop(ra, 1<<3)
loop(rb, 1<<3)

loop(i, 4)
	((aluop+i)<<12 | rd<<8 | ra<<4 | rb<<0) 0  #test add/sub/and/orr
end loop

	(ldrop    <<12 | rd<<8 | ra<<4 )        1  #test ldr
	
	let imm = random(256);
	(movlop   <<12 | rd<<8 | imm )          2  #test movl

end loop
end loop
end loop
*/
