// Digital circuit cpu.dig as structural Verilog
module cpu (
  input  CLK,
  output Z,
  output N,
  output C,
  output V
);

  wire control_unit_1_ldr, control_unit_1_str, control_unit_1_we;
  wire [1:0] control_unit_1_aluop, control_unit_1_dmux;
  wire [2:0] control_unit_1_rs1, control_unit_1_rs2, control_unit_1_ws;
  wire [7:0] RAM_d2;
  wire [15:0] alu_1_result, multiplexer_1_out, notconnected_1_out, PC_q, plus_1_s, RAM_d1, reg_file_1_out1,
       reg_file_1_out2;
  wire [15:8] RAM_d2_2;

  // Probe ALUOP on control_unit_1_aluop
  control_unit control_unit_1 (
    .INST({RAM_d2_2, RAM_d2}), .ALUOP(control_unit_1_aluop), .DMUX(control_unit_1_dmux),
    .RS1(control_unit_1_rs1), .RS2(control_unit_1_rs2), .WS(control_unit_1_ws), .WE(control_unit_1_we),
    .STR(control_unit_1_str), .LDR(control_unit_1_ldr));
  Multiplexer #(.Selector_Bits(2), .Bits(16)) multiplexer_1 (
    .sel(control_unit_1_dmux), .in_0(alu_1_result), .in_1(RAM_d1), .in_2({{8{1'b0}}, RAM_d2}),
    .in_3(notconnected_1_out), .out(multiplexer_1_out));
  // NotConnected on notconnected_1_out
  // Probe IN on {{8{1'b0}}, RAM_d2}
  // Probe DMUX on control_unit_1_dmux
  RAMDualAccess #(.AddrBits(16), .Bits(16)) RAM (
    .str(control_unit_1_str), .C(CLK), .ld(control_unit_1_ldr), .A1(reg_file_1_out1), .Din1(reg_file_1_out2),
    .A2(PC_q), .D1(RAM_d1), .D2({RAM_d2_2, RAM_d2}));
  // Probe DATA on multiplexer_1_out
  reg_file reg_file_1 (
    .IN(multiplexer_1_out), .clk(CLK), .RS1(control_unit_1_rs1), .RS2(control_unit_1_rs2),
    .WS(control_unit_1_ws), .WE(control_unit_1_we), .OUT1(reg_file_1_out1), .OUT2(reg_file_1_out2));
  Register #(.Bits(16), .isProgramCounter("true")) PC (.D(plus_1_s), .C(CLK), .en(1'b1), .Q(PC_q));
  Add #(.Bits(16)) plus_1 (.a(16'h1), .b(PC_q), .c_i(1'b0), .s(plus_1_s));  // open: c_o
  // Probe RS1 on control_unit_1_rs1
  // Probe WS on control_unit_1_ws
  // Probe RS2 on control_unit_1_rs2
  // Probe WE on control_unit_1_we
  alu alu_1 (
    .A(reg_file_1_out1), .B(reg_file_1_out2), .RESULT(alu_1_result), .ALUOP(control_unit_1_aluop),
    .FLAG({V, C, N, Z}));
endmodule
