// Digital circuit reg_file.dig as structural Verilog
module reg_file (
  input  [15:0] IN,
  input  clk,
  input  WE,
  input  [2:0] WS,
  input  [2:0] RS1,
  input  [2:0] RS2,
  input  [15:0] FLIN,
  input  EXEC,
  input  SETH,
  output [15:0] OUT1,
  output [15:0] OUT2,
  output [15:0] PC
);

  wire and_1_out, demultiplexer_1_out_1, demultiplexer_1_out_2, demultiplexer_1_out_3, demultiplexer_1_out_4,
       demultiplexer_1_out_7;
  wire [15:0] multiplexer_1_out, notconnected_1_out, notconnected_2_out, plus_1_s, R1_q, R2_q, R3_q, R4_q,
       seth_1_d, seth_2_d, seth_3_d, seth_4_d, seth_5_d;

  Demultiplexer #(.Selector_Bits(3)) demultiplexer_1 (
    .sel(WS), .in(WE), .out_1(demultiplexer_1_out_1), .out_2(demultiplexer_1_out_2),
    .out_3(demultiplexer_1_out_3), .out_4(demultiplexer_1_out_4), .out_7(demultiplexer_1_out_7));  // open: out_0, out_5, out_6
  and and_1 (and_1_out, demultiplexer_1_out_7, EXEC);
  Multiplexer #(.Bits(16)) multiplexer_1 (.sel(and_1_out), .in_0(plus_1_s), .in_1(seth_5_d), .out(multiplexer_1_out));
  Register #(.Bits(16)) R1 (.D(seth_1_d), .C(clk), .en(demultiplexer_1_out_1), .Q(R1_q));
  Register #(.Bits(16)) R2 (.D(seth_2_d), .C(clk), .en(demultiplexer_1_out_2), .Q(R2_q));
  Register #(.Bits(16)) R3 (.D(seth_3_d), .C(clk), .en(demultiplexer_1_out_3), .Q(R3_q));
  Register #(.Bits(16)) R4 (.D(seth_4_d), .C(clk), .en(demultiplexer_1_out_4), .Q(R4_q));
  Register #(.Bits(16), .isProgramCounter("true")) u_PC (.D(multiplexer_1_out), .C(clk), .en(1'b1), .Q(PC));
  seth seth_1 (.IN(IN), .SETH(SETH), .Q(R1_q), .D(seth_1_d));
  seth seth_2 (.IN(IN), .SETH(SETH), .Q(R2_q), .D(seth_2_d));
  seth seth_3 (.IN(IN), .SETH(SETH), .Q(R3_q), .D(seth_3_d));
  seth seth_4 (.IN(IN), .SETH(SETH), .Q(R4_q), .D(seth_4_d));
  seth seth_5 (.IN(IN), .SETH(SETH), .Q(PC), .D(seth_5_d));
  Add #(.Bits(16)) plus_1 (.a(16'h1), .b(PC), .c_i(1'b0), .s(plus_1_s));  // open: c_o
  Multiplexer #(.Selector_Bits(3), .Bits(16)) multiplexer_2 (
    .sel(RS1), .in_0({16{1'b0}}), .in_1(R1_q), .in_2(R2_q), .in_3(R3_q), .in_4(R4_q), .in_5(FLIN),
    .in_6(notconnected_2_out), .in_7(PC), .out(OUT1));
  // NotConnected on notconnected_1_out
  // NotConnected on notconnected_2_out
  Multiplexer #(.Selector_Bits(3), .Bits(16)) multiplexer_3 (
    .sel(RS2), .in_0({16{1'b0}}), .in_1(R1_q), .in_2(R2_q), .in_3(R3_q), .in_4(R4_q), .in_5(FLIN),
    .in_6(notconnected_1_out), .in_7(PC), .out(OUT2));

  // Notes on the sheet:
  //   IN: The value to be saved into the register specified by WS if WE is high,
  //   WE: Whether the register selected by WS should save the value from IN on the next cycle.
  //   WS: The index of the register which should save the value on IN on the next clock cycle (if WE is high).
  //   RS1: The index of the register which should output its value to OUT1.
  //   OUT1: The value in the register specified by RS1.
  //   OUT2: The value in the register specified by RS2.
  //   RS2: The index of the register which should output its value to OUT2.
endmodule

/* Test case:
clk RS1 RS2 WS WE IN OUT1 OUT2
c 4 4 4 1 0x1234 0x1234 0x1234
c 1 4 1 1 0xBEEF 0xBEEF 0x1234
c 2 1 2 1 0xDEAD 0xDEAD 0xBEEF
c 3 2 3 1 0xFFFF 0xFFFF 0xDEAD
c 3 2 3 0 0xABCD 0xFFFF 0xDEAD
c 3 2 2 0 0xABCD 0xFFFF 0xDEAD
c 1 4 1 0 0xABCD 0xBEEF 0x1234
c 1 4 4 0 0xABCD 0xBEEF 0x1234
c 1 4 2 1 0xBADE 0xBEEF 0x1234
c 4 2 2 1 0xBADE 0x1234 0xBADE
c 4 4 2 0 0x1234 0x1234 0x1234
c 2 3 4 1 0x0000 0xBADE 0xFFFF
c 4 4 2 0 0x1234 0x0000 0x0000
*/
