// Digital circuit seth.dig as structural Verilog
module seth (
  input  [15:0] IN,
  input  [15:0] Q,
  input  SETH,
  output [15:0] D
);

  Multiplexer #(.Bits(16)) multiplexer_1 (.sel(SETH), .in_0(IN), .in_1({IN[7:0], Q[7:0]}), .out(D));
endmodule

/* Test case:
SETH IN Q D
1 0x34 0x12 0x3412
0 0x34 0x12 0x34
*/
